# Fritzing sketch DHT11 (saved by Fritzing 0.9.3b)
circuit board: 8.46667cm x 5.64444cm
breadboards: 1

parts:
  DHT1 = DHT11 Humitidy and Temperature Sensor
  Componente1 = Arduino Uno (Rev3)
  R1 = Resistor [tolerance=±5% resistance=4.7k package=THT]

nets:
  VDD: DHT1.VDD, Componente1.5V, R1.Pin_0
  N1: DHT1.DATA, Componente1.D2, R1.Pin_1
  GND: DHT1.GND, Componente1.GND

custom parts:
  DHT11 Humitidy and Temperature Sensor: DHT11 Humidity and Temperature Sensor

// code stored in the sketch: DTH11.ino
#include <DHT.h>//se incluye la librería
 
// Definimos el pin digital donde se conecta el sensor
#define DHTPIN 2
// Dependiendo del tipo de sensor
#define DHTTYPE DHT11
 
// Inicializamos el sensor DHT11
DHT dht(DHTPIN, DHTTYPE);
 
void setup() {
  // Inicializamos comunicaci?n serie
  Serial.begin(9600);
 
  // Comenzamos el sensor DHT
  dht.begin();
 
}
 
void loop() {
    // Esperamos 5 segundos entre medidas
  delay(5000);
 
  // Leemos la humedad relativa
  float h = dht.readHumidity();
  // Leemos la temperatura en grados cent?grados (por defecto)
  float t = dht.readTemperature();
  // Leemos la temperatura en grados Fahreheit
  float f = dht.readTemperature(true);
 
  // Comprobamos si ha habido alg?n error en la lectura
  if (isnan(h) || isnan(t) || isnan(f)) {
    Serial.println("Error obteniendo los datos del sensor DHT11");
    return;
  }
 
  // Calcular el ?ndice de calor en Fahreheit
  float hif = dht.computeHeatIndex(f, h);
  // Calcular el ?ndice de calor en grados cent?grados
  float hic = dht.computeHeatIndex(t, h, false);
 
  Serial.print("Humedad: ");
  Serial.print(h);
  Serial.print(" %\t");
  Serial.print("Temperatura: ");
  Serial.print(t);
  Serial.print(" *C ");
  Serial.print(f);
  Serial.print(" *F\t");
  Serial.print("?ndice de calor: ");
  Serial.print(hic);
  Serial.print(" *C ");
  Serial.print(hif);
  Serial.println(" *F");
 
}
