# Fritzing sketch LM35 (saved by Fritzing 0.9.3b)
circuit board: 8.46667cm x 5.64444cm
breadboards: 1

parts:
  Componente1 = Arduino Uno (Rev3)
  T1 = LM35 Temperature Sensor [package="TO92 [THT]"]

nets:
  N1: Componente1.A0, T1.Vout
  GND: Componente1.GND, T1.GND
  N2: Componente1.5V, T1.+Vs

// code stored in the sketch: LM35.ino
int SENSOR_LM=A0;//Se nombra el pin que leerá el sensor
float temperatura = 0; //variable para la temperatura

void setup(){
Serial.begin (9600); //se inicia comunicacion serial
}
 
void loop(){
temperatura=(analogRead(SENSOR_LM)*500)/1023;//se hace la conversión para obtener la temperatura real
Serial.println (temperatura);//se imprime la temperatura en el puerto serial
delay (1000); //cada segundo se imprime una nueva temperatura
}
